# Fritzing sketch FT (saved by Fritzing 0.9.3b)
breadboards: 1

parts:
  부품1 = Arduino Uno (Rev3)
  Power_plug1 = Power plug
  U2 = 4-Channel 5v Relay Shield [package=relay-4ch5v10a]
  U3 = 4-Channel 5v Relay Shield [package=relay-4ch5v10a]
  L1 = Solenoid
  L2 = Solenoid
  BT1 = Bluetooth HC-06u [package=THT]
  L3 = Solenoid
  L5 = Solenoid
  L4 = Solenoid
  L6 = Solenoid
  L7 = Solenoid
  L8 = Solenoid

nets:
  N1: 부품1.D8, U2.IN1
  N2: 부품1.D9_PWM, U2.IN2
  N3: 부품1.D10_PWM/SS, U2.IN3
  N4: 부품1.D11_PWM/MOSI, U2.IN4
  N5: 부품1.D0/RX, BT1.TXD
  N6: 부품1.D1/TX, BT1.RXD
  GND: 부품1.D4, 부품1.GND, Power_plug1.GND, U2.GND, U3.GND, U3.IN1, L1.pin1, L2.pin1, BT1.GND, L3.pin1, L5.pin1, L4.pin1, L6.pin1, L7.pin1, L8.pin1
  N7: 부품1.D5_PWM, U3.IN2
  N8: 부품1.D6_PWM, U3.IN3
  N9: 부품1.D7, U3.IN4
  VCC: 부품1.5V, Power_plug1.VCC, U2.VCC, U2.K1-Off, U2.K2-Off, U2.K3-Off, U2.K4-Off, U3.VCC, U3.K1-Off, U3.K2-Off, U3.K3-Off, U3.K4-Off, BT1.VCC
  N10: U2.K1-On, L5.pin2
  N11: U2.K2-On, L6.pin2
  N12: U2.K3-On, L7.pin2
  N13: U2.K4-On, L8.pin2
  N14: U3.K1-On, L4.pin2
  N15: U3.K2-On, L3.pin2
  N16: U3.K3-On, L2.pin2
  N17: U3.K4-On, L1.pin2

notes:
  INPUT 5V
  Electromagnet
  Bluetooth Module
  4ch Relay
  Arduino Uno

custom parts:
  4-Channel 5v Relay Shield: 4 Channel 5v Relay Shield w. 2x SPD-06VDC-SD-C
  Bluetooth HC-06u: Bluetooth HC-06 - face up, pins down 16.5mm x 37.5mm PCB
