# Fritzing sketch KP (saved by Fritzing 0.9.3b)
breadboards: 1

parts:
  U1 = 16-Channel Relay Module [package=relay-16ch]
  U2 = 16-Channel Relay Module [package=relay-16ch]
  BT1 = Bluetooth HC-06u [package=THT]
  Power_plug1 = Power plug
  L1 = Solenoid
  L2 = Solenoid
  L3 = Solenoid
  L4 = Solenoid
  L5 = Solenoid
  L6 = Solenoid
  L7 = Solenoid
  L8 = Solenoid
  L9 = Solenoid
  L10 = Solenoid
  L12 = Solenoid
  부품2 = Arduino Mega 2560 (Rev3)
  L11 = Solenoid

nets:
  VCC: U1.VCC, U2.VCC, Power_plug1.VCC
  GND: U1.GND, U1.OUT_GND, U2.GND, Power_plug1.GND
  N1: U1.IN2, 부품2.D36
  N2: U1.IN4, 부품2.D34
  N3: U1.IN6, 부품2.D32
  N4: U1.IN7, 부품2.D46
  N5: U1.IN8, 부품2.D30
  N6: U1.IN9, 부품2.D44
  N7: U1.IN10, 부품2.D28
  N8: U1.IN11, 부품2.D42
  N9: U1.IN12, 부품2.D26
  N10: U1.IN13, 부품2.D40
  N11: U1.IN14, 부품2.D24
  N12: U1.IN15, 부품2.D38
  N13: U1.IN16, 부품2.D22
  N14: U1.K1_NO, L1.pin2, L2.pin2, L3.pin2, L4.pin2, L5.pin2, L6.pin2
  GND_2: U1.K1_COM, U2.K16_COM, BT1.GND, L1.pin1, L2.pin1, L3.pin1, L4.pin1, L5.pin1, L6.pin1, L7.pin1, L8.pin1, L9.pin1, L10.pin1, L12.pin1, 부품2.GND, L11.pin1
  N15: U2.IN1, 부품2.D39
  N16: U2.IN2, 부품2.D23
  N17: U2.IN3, 부품2.D41
  N18: U2.IN4, 부품2.D25
  N19: U2.IN5, 부품2.D43
  N20: U2.IN6, 부품2.D27
  N21: U2.IN7, 부품2.D45
  N22: U2.IN8, 부품2.D29
  N23: U2.IN9, 부품2.D47
  N24: U2.IN10, 부품2.D31
  N25: U2.IN12, 부품2.D33
  N26: U2.IN14, 부품2.D35
  N27: U2.IN16, 부품2.D37
  N28: U2.K16_NO, L8.pin2, L9.pin2, L10.pin2
  VCC_2: BT1.VCC, 부품2.5V
  N29: BT1.TXD, 부품2.D19/RX1
  N30: BT1.RXD, 부품2.D18/TX1
  N31: L12.pin2, L11.pin2

notes:
  Arduino Mega
  INPUT 12V
  Bluetooth Module
  Electromagnet X 26
  16ch Relay

custom parts:
  16-Channel Relay Module: 16 channel relay module
  Bluetooth HC-06u: Bluetooth HC-06 - face up, pins down 16.5mm x 37.5mm PCB
